# Fritzing sketch buggy (saved by Fritzing 0.7.5b)
breadboards: 1

parts:
  RaspberryPi1 = Raspberry Pi Model B
  IC1 = L293D [package=THT]  # not connected
  M1 = DC Motor  # not connected
  M2 = DC Motor  # not connected
  VCC2 = 4 x AAA Battery Mount

nets:
  N1: RaspberryPi1.GND, VCC2.-

custom parts:
  Raspberry Pi Model B: Raspberry Pi (Model B)
